# Fritzing sketch midicontroller (saved by Fritzing 0.9.3b)

parts:
  Part1 = Arduino Uno (Rev3)
  Sparkfun_74HC4051 = 74HC4051 [package=so16]
  Sparkfun_CD74HC4067 = Analog Digital MUX Breakout
  FX_1 = Pushbutton [package="[THT]"]
  Cue_A = Pushbutton [package="[THT]"]
  Play_Pause_A = Pushbutton [package="[THT]"]
  Play/Pause_B = Pushbutton [package="[THT]"]
  Cue_B = Pushbutton [package="[THT]"]
  FX_2 = Pushbutton [package="[THT]"]
  High_A = Rotary Potentiometer (Small) [maximum_resistance=10kΩ package=THT]
  Mid_A = Rotary Potentiometer (Small) [maximum_resistance=10kΩ package=THT]
  Low_A = Rotary Potentiometer (Small) [maximum_resistance=10kΩ package=THT]
  High_B = Rotary Potentiometer (Small) [maximum_resistance=10kΩ package=THT]
  Mid_B = Rotary Potentiometer (Small) [maximum_resistance=10kΩ package=THT]
  Low_B = Rotary Potentiometer (Small) [maximum_resistance=10kΩ package=THT]
  Master_Volume = Rotary Potentiometer (Small) [maximum_resistance=10kΩ package=THT]
  Channel_B = Slide Potentiometer [maximum_resistance=10kΩ]
  Crossfader = Slide Potentiometer [maximum_resistance=50kΩ]
  Channel_A = Slide Potentiometer [maximum_resistance=10kΩ]
  FX_1_LED = LED - 5mm [color="Red (633nm)" package="5 mm [THT]"]
  Play_pause_LED_B = LED - 5mm [color="Red (633nm)" package="5 mm [THT]"]
  Cue_LED_B = LED - 5mm [color="Red (633nm)" package="5 mm [THT]"]
  FX_2_LED = LED - 5mm [color="Red (633nm)" package="5 mm [THT]"]
  R1 = Resistor [tolerance=±5% resistance=330 package=THT]
  R2 = Resistor [tolerance=±5% resistance=330 package=THT]
  R3 = Resistor [tolerance=±5% resistance=330 package=THT]
  R4 = Resistor [tolerance=±5% resistance=330 package=THT]
  R5 = Resistor [tolerance=±5% resistance=330 package=THT]
  R6 = Resistor [tolerance=±5% resistance=330 package=THT]
  Cue_LED_A = LED - 5mm [color="Red (633nm)" package="5 mm [THT]"]
  Play_pause_LED_A = LED - 5mm [color="Red (633nm)" package="5 mm [THT]"]

nets:
  N1: Part1.A0, Sparkfun_CD74HC4067.SIG
  N2: Part1.D8, Sparkfun_74HC4051.A, Sparkfun_CD74HC4067.S0
  N3: Part1.D9_PWM, Sparkfun_74HC4051.B, Sparkfun_CD74HC4067.S1
  N4: Part1.D10_PWM/SS, Sparkfun_74HC4051.C, Sparkfun_CD74HC4067.S2
  N5: Part1.D11_PWM/MOSI, Sparkfun_CD74HC4067.S3
  N6: Part1.D12/MISO, Sparkfun_74HC4051.IO
  GND: Part1.GND, Sparkfun_74HC4051.VSS, Sparkfun_CD74HC4067.GND, FX_1.Pin_1, FX_1.Pin_2, Cue_A.Pin_1, Cue_A.Pin_2, Play_Pause_A.Pin_1, Play_Pause_A.Pin_2, Play/Pause_B.Pin_1, Play/Pause_B.Pin_2, Cue_B.Pin_1, Cue_B.Pin_2, FX_2.Pin_1, FX_2.Pin_2, High_A.leg1, Mid_A.leg1, Low_A.leg1, High_B.leg1, Mid_B.leg1, Low_B.leg1, Master_Volume.leg1, Channel_B.leg1, Crossfader.leg1, Channel_A.leg1, FX_1_LED.cathode, Play_pause_LED_B.cathode, Cue_LED_B.cathode, FX_2_LED.cathode, Cue_LED_A.cathode, Play_pause_LED_A.cathode
  N7: Part1.D2, R6.Pin_0
  N8: Part1.D3_PWM, R5.Pin_0
  N9: Part1.D4, R1.Pin_0
  N10: Part1.D5_PWM, R2.Pin_0
  N11: Part1.D6_PWM, R3.Pin_0
  N12: Part1.D7, R4.Pin_0
  5V: Part1.5V, Sparkfun_74HC4051.VDD, Sparkfun_CD74HC4067.VCC, High_A.leg2, Mid_A.leg2, Low_A.leg2, High_B.leg2, Mid_B.leg2, Low_B.leg2, Master_Volume.leg2, Channel_B.leg2, Crossfader.leg2, Channel_A.leg2
  N13: Sparkfun_74HC4051.IO4, Cue_B.Pin_4
  N14: Sparkfun_74HC4051.IO5, FX_2.Pin_3, FX_2.Pin_4
  N15: Sparkfun_74HC4051.IO3, Play/Pause_B.Pin_4
  N16: Sparkfun_74HC4051.IO0, Play_Pause_A.Pin_3, Play_Pause_A.Pin_4
  N17: Sparkfun_74HC4051.IO1, Cue_A.Pin_3, Cue_A.Pin_4
  N18: Sparkfun_74HC4051.IO2, FX_1.Pin_3, FX_1.Pin_4
  N19: Sparkfun_CD74HC4067.C0, Low_A.wiper
  N20: Sparkfun_CD74HC4067.C1, Mid_A.wiper
  N21: Sparkfun_CD74HC4067.C2, High_A.wiper
  N22: Sparkfun_CD74HC4067.C3, Channel_A.wiper
  N23: Sparkfun_CD74HC4067.C4, High_B.wiper
  N24: Sparkfun_CD74HC4067.C5, Mid_B.wiper
  N25: Sparkfun_CD74HC4067.C6, Low_B.wiper
  N26: Sparkfun_CD74HC4067.C7, Channel_B.wiper
  N27: Sparkfun_CD74HC4067.C8, Crossfader.wiper
  N28: Sparkfun_CD74HC4067.C9, Master_Volume.wiper
  N29: FX_1_LED.anode, R1.Pin_1
  N30: Play_pause_LED_B.anode, R2.Pin_1
  N31: Cue_LED_B.anode, R3.Pin_1
  N32: FX_2_LED.anode, R4.Pin_1
  N33: R5.Pin_1, Cue_LED_A.anode
  N34: R6.Pin_1, Play_pause_LED_A.anode

notes:
  LEDs / resistors for example. Actual project contains LEDs built into the buttons.
